# Fritzing sketch Robot_v1 (saved by Fritzing 0.9.6b)
breadboards: 2

parts:
  Part1 = Arduino Uno (Rev3)
  HC-SR04_Sensor_1 = HC-SR04 Ultrasonic Distance Sensor
  Part2 = Arduino Nano (Rev3.0)
  Part5 = NRF24L01+ Breakout Board
  Part6 = Black Joystick KY-023
  Part7 = NRF24L01+ Breakout Board
  IR1 = TSOP312.., 314.. [package=THT]
  Q1 = MOSFET-NCHANNEL [package=to220v]
  Q2 = MOSFET-NCHANNEL [package=to220v]
  BAT1 = BC9VPC [package=bc9vpc]
  M1 = gear-motor
  M2 = gear-motor
  M3 = gear-motor
  M4 = gear-motor

nets:
  N1: Part1.D8, Part7.CS
  N2: Part1.D9_PWM, Q2.G
  N3: Part1.D10_PWM/SS, Q1.G
  N4: Part1.D11_PWM/MOSI, Part7.MOSI
  N5: Part1.D12/MISO, Part7.MISO
  N6: Part1.D13/SCK, Part7.SCK
  GND: Part1.GND, HC-SR04_Sensor_1.GND, Part7.GND, IR1.GND
  N7: Part1.D2, HC-SR04_Sensor_1.ECHO
  N8: Part1.D3_PWM, HC-SR04_Sensor_1.TRIG
  N9: Part1.D4, IR1.Data
  N10: Part1.D7, Part7.CE
  3V3: Part1.3V3, Part7.VCC
  5V: Part1.5V, HC-SR04_Sensor_1.VCC, IR1.Vs
  GND_2: Part2.GND, Part5.GND, Part6.GND
  N11: Part2.D7, Part5.CE
  N12: Part2.D8, Part5.CS
  N13: Part2.D11/MOSI, Part5.MOSI
  N14: Part2.D12/MISO, Part5.MISO
  5V_2: Part2.5V, Part6.+5V
  N15: Part2.A1, Part6.VRy
  N16: Part2.A0, Part6.VRx
  3V3_2: Part2.3V3, Part5.VCC
  N17: Part2.D13/SCK, Part5.SCK
  N18: Q1.D, M1.pin_1, M2.pin_1
  N19: Q1.S, Q2.S, BAT1.V-
  N20: Q2.D, M3.pin_1, M4.pin_1
  N21: BAT1.V+, M1.pin_2, M2.pin_2, M3.pin_2, M4.pin_2

notes:
  This ultasonc sensor will be placed on the front of the cart to enssure that collisions do not occur
  For comunication between the remote and the robot
  This will be the remote control for the robot if I revive an rf module on time

custom parts:
  Black Joystick KY-023: Description: The joystick is a combination of 2 analoog potentiometer and a digital switch. Arduino GND --> Module pin - Arduino +5V --> Module pin +5V Arduino Analoog 0 --> Module VRx Arduino Analoog 1 --> Module VRy Arduino Digital --> Module SW Dimensions: 1" x 1.25"
